# Fritzing sketch breadboard (saved by Fritzing 1.0.2b)
breadboards: 1

parts:
  GameCube = Raspberry Pi Pico
  Bluetooth_(Pico_W) = Raspberry Pi Pico

nets:
  N1: GameCube.pin_3, GameCube.pin_8, GameCube.pin_13, GameCube.pin_18, GameCube.pin_23, GameCube.pin_28, GameCube.pin_32, GameCube.pin_33, GameCube.pin_38, GameCube.pin_39, Bluetooth_(Pico_W).pin_3, Bluetooth_(Pico_W).pin_8, Bluetooth_(Pico_W).pin_13, Bluetooth_(Pico_W).pin_18, Bluetooth_(Pico_W).pin_23, Bluetooth_(Pico_W).pin_28, Bluetooth_(Pico_W).pin_33, Bluetooth_(Pico_W).pin_38, Bluetooth_(Pico_W).pin_39, Bluetooth_(Pico_W).pin_42
  N2: GameCube.pin_21, Bluetooth_(Pico_W).pin_26
  N3: GameCube.pin_22, Bluetooth_(Pico_W).pin_22
  N4: GameCube.pin_24, Bluetooth_(Pico_W).pin_25
  N5: GameCube.pin_25, Bluetooth_(Pico_W).pin_21

custom parts:
  Raspberry Pi Pico: Raspberry Pi Pico. Based around the RP2040 microcontroller the Pico is a low cost microcontroller device bringing Raspberry Pi quality, cost, and easy of use to the microcontroller space. Jan 2021, Split part in to two versions: tht (this one) and SMD. This one will drill holes for a .1 in header in pcb to allow plugging in the module as well as providing pads to solder the module to the top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
